// Logisim project ProjetIntegrateur.circ as structural Verilog: 1 circuit, main circuit main
// Test
module main (
  input  G,
  input  MG,
  input  MD,
  input  D,
  output EG,
  output G_2,
  output D_2,
  output ED
);

  wire not_1_out, not_2_out, or_1_out, or_2_out;

  or or_1 (or_1_out, G, D, MD);
  not not_1 (not_1_out, or_1_out);
  or or_2 (or_2_out, G, D, MG);
  not not_2 (not_2_out, or_2_out);
  and and_1 (G_2, not_1_out, not_1_out, MG);
  and and_2 (D_2, MD, not_2_out);

  assign ED = D;
  assign EG = G;
endmodule
