// Logisim project ProjetIntegrateur.circ as structural Verilog: 1 circuit, main circuit main
// Test
module main (
  input  EG,
  input  G,
  input  D,
  input  ED,
  output G_2,
  output MG,
  output MD,
  output D_2
);

  wire not_1_out, not_2_out, or_1_out, or_2_out;

  or or_1 (or_1_out, EG, ED, D);
  not not_1 (not_1_out, or_1_out);
  not not_2 (not_2_out, or_2_out);
  or or_2 (or_2_out, EG, ED, G);
  and and_1 (MG, not_1_out, not_1_out, G);
  and and_2 (MD, D, not_2_out);

  assign D_2 = ED;
  assign G_2 = EG;
endmodule
